// Logisim project pcb_computer.circ as structural Verilog: 11 circuits, main circuit main
module main (
);

  wire Clk, Count, fixed74181_1_cout, NotClearMicrocode, NotEnableA16, NotEnableAHigh, NotEnableALow,
       NotEnableB, NotEnableC, NotEnableIRHigh, NotEnableIRLow, NotEnablePC16, NotEnableRam, NotLoadAHigh,
       NotLoadALow, NotLoadB, NotLoadC, NotLoadIRHigh, NotLoadIRLow, NotLoadPC, NotLoadRam;
  wire [1:0] microcode_1_a;
  wire [3:0] fixed74181_1_y1, rom_2_data;
  wire [7:0] Bus8, IRLow_dataout, programcounter_1_addressout, programcounter_1_addressout_2,
       ram_idt7134_1_dataoutr;
  wire [15:0] ALow_dataout, memoryhelper_1_ramaddress;

  // Probe on fixed74181_1_cout
  fixed74181 fixed74181_1 (
    .COUT(fixed74181_1_cout), .Y4(fixed74181_1_y1[3]), .Y3(fixed74181_1_y1[2]), .Y2(fixed74181_1_y1[1]),
    .Y1(fixed74181_1_y1[0]), .S4(1'b0), .S1(1'b0), .B4(1'b0), .A4(1'b1), .B3(1'b0), .S2(1'b1), .A3(1'b0),
    .B2(1'b0), .A2(1'b0), .B1(1'b0), .S3(1'b1), .A1(1'b0), .M(1'b0), .CIN(1'b1));  // open: P, G, EQ
  // Probe on Bus8
  Clock clock_1 (.out(Clk));
  // Probe on fixed74181_1_y1
  Microcode microcode_1 (.NotClear(NotClearMicrocode), .Clock(Clk), .A(microcode_1_a[0]), .B(microcode_1_a[1]));
  Register8 IRHigh (
    .Clock(Clk), .NotLoad(NotLoadIRHigh), .NotEnable(NotEnableIRHigh), .BusIn(Bus8), .BusOut(Bus8));  // open: DataOut
  Register8 IRLow (
    .Clock(Clk), .NotLoad(NotLoadIRLow), .NotEnable(NotEnableIRLow), .BusIn(Bus8), .BusOut(Bus8),
    .DataOut(IRLow_dataout));
  Register8 AHigh (
    .Clock(Clk), .NotLoad(NotLoadAHigh), .NotEnable(NotEnableAHigh), .BusIn(Bus8), .BusOut(Bus8),
    .DataOut(ALow_dataout[15:8]));
  Register8 ALow (
    .Clock(Clk), .NotLoad(NotLoadALow), .NotEnable(NotEnableALow), .BusIn(Bus8), .BusOut(Bus8),
    .DataOut(ALow_dataout[7:0]));
  Register8 B (.Clock(Clk), .NotLoad(NotLoadB), .NotEnable(NotEnableB), .BusIn(Bus8), .BusOut(Bus8));  // open: DataOut
  Register8 C (.Clock(Clk), .NotLoad(NotLoadC), .NotEnable(NotEnableC), .BusIn(Bus8), .BusOut(Bus8));  // open: DataOut
  ROM #(.addrWidth(11), .dataWidth(19)) rom_1 (
    .addr({microcode_1_a, 9'h48}),
    .data({NotEnableRam, NotLoadRam, NotClearMicrocode, Count, NotLoadPC, NotEnableA16, NotEnablePC16, NotEnableC, NotLoadC, NotEnableB, NotLoadB, NotEnableALow, NotEnableAHigh, NotLoadALow, NotLoadAHigh, NotEnableIRLow, NotEnableIRHigh, NotLoadIRLow, NotLoadIRHigh}));
  // Probe on {microcode_1_a, 9'h48}
  ROM #(.addrWidth(15), .dataWidth(4)) rom_2 (.addr(15'h1), .data(rom_2_data));
  ProgramCounter programcounter_1 (
    .Clock(Clk), .NotClear(1'b1), .NotLoad(NotLoadPC), .Count(Count), .AddressIn(ALow_dataout),
    .AddressOut({programcounter_1_addressout_2, programcounter_1_addressout}));
  MemoryHelper memoryhelper_1 (
    .NotEnablePC(NotEnablePC16), .PCHigh(programcounter_1_addressout_2), .PCLow(programcounter_1_addressout),
    .NotEnableA(NotEnableA16), .AHigh(ALow_dataout[15:8]), .ALow(ALow_dataout[7:0]),
    .RAMAddress(memoryhelper_1_ramaddress));
  // Probe on {programcounter_1_addressout_2, programcounter_1_addressout}
  // Probe on memoryhelper_1_ramaddress[1:0]
  RAM_IDT7134 ram_idt7134_1 (
    .Clock(Clk), .DataInL(Bus8), .NotWriteRamL(NotLoadRam), .AddressL(memoryhelper_1_ramaddress[1:0]),
    .AddressR(2'b00), .NotOutputEnableL(NotEnableRam), .NotOutputEnableR(1'b0), .DataOutL(Bus8),
    .DataOutR(ram_idt7134_1_dataoutr));
  // Probe on Bus8
  // Probe on ram_idt7134_1_dataoutr

  // Notes on the sheet:
  //   contents of rom_1 (hex, n*v repeats v):
  //   512*3effd 512*36ffe 8*6efff 8*6efef 8*6efdf 8*6eeff 8*6ebff 8*4efff 16*6efff 8*6efbf 8*6efaf 8*6ef9f
  //   8*6eebf 8*6ebbf 8*4efbf 16*6efbf 8*6ef7f 8*6ef6f 8*6ef5f 8*6ee7f 8*6eb7f 8*4ef7f 16*6ef7f 8*6edff
  //   8*6edef 8*6eddf 8*6ecff 8*6e9ff 8*4edff 16*6edff 8*6e7ff 8*6e7ef 8*6e7df 8*6e6ff 8*6e3ff 8*4e7ff
  //   16*6e7ff 8*2efff 8*2efef 8*2efdf 8*2eeff 8*2ebff 8*efff 16*2efff 8*6effb 8*6efeb 8*6efdb 8*6eefb
  //   8*6ebfb 8*4effb 16*6effb 8*6efff 8*6efef 8*6efdf 8*6eeff 8*6ebff 8*4efff 16*6efff 8*7efff 8*7efef
  //   8*7efdf 8*7eeff 8*7ebff 8*5efff 16*7efff 8*7efbf 8*7efaf 8*7ef9f 8*7eebf 8*7ebbf 8*5efbf 16*7efbf
  //   8*7ef7f 8*7ef6f 8*7ef5f 8*7ee7f 8*7eb7f 8*5ef7f 16*7ef7f 8*7edff 8*7edef 8*7eddf 8*7ecff 8*7e9ff
  //   8*5edff 16*7edff 8*7e7ff 8*7e7ef 8*7e7df 8*7e6ff 8*7e3ff 8*5e7ff 16*7e7ff 8*3efff 8*3efef 8*3efdf
  //   8*3eeff 8*3ebff 8*1efff 16*3efff 8*7effb 8*7efeb 8*7efdb 8*7eefb 8*7ebfb 8*5effb 16*7effb 8*7efff
  //   8*7efef 8*7efdf 8*7eeff 8*7ebff 8*5efff 16*7efff
  //   contents of rom_2 (hex, n*v repeats v):
  //   d d f f d d f f d d f f d d f f d d f f d d f f d d f f d d f f d d f f d d f f d d f f d d f f d d
  //   f f d d f f d d f f d d f f d d f f d d f f d d f f d d f f d d f f d d f f d d f f d d f f d d f f
  //   d d f f d d f f d d f f d d f f d d f f d d f f d d f f d d f f d d f f d d f f d d f f d d f f d d
  //   f f d d f f d d f f d d f f d d f f d d f f d d f f d d f f d d f f d d f f d d f f d d f f d d f f
  //   d d f f d d f f d d f f d d f f d d f f d d f f d d f f d d f f d d f f d d f f d d f f d d f f d d
  //   f f d d f f d d f f d d f f d d f f d d f f d d f f d d f f d d f f d d f f d d f f d d f f d d f f
  //   d d f f d d f f d d f f d d f f d d f f d d f f d d f f d d f f d d f f d d f f d d f f d d f f d d
  //   f f d d f f d d f f d d f f d d f f d d f f d d f f d d f f d d f f d d f f d d f f d d f f d d f f
  //   d d f f d d f f d d f f d d f f d d f f d d f f d d f f d d f f d d f f d d f f d d f f d d f f d d
  //   f f d d f f d d f f d d f f d d f f d d f f d d f f d d f f d d f f d d f f d d f f d d f f d d f f
  //   d d f f d d f f d d f f d d f f d d f f d d f f d d f f d d f f d d f f d d f f d d f f d d f f d d
  //   f f d d f f d d f f d d f f d d f f d d f f d d f f d d f f d d f f d d f f d d f f d d f f d d f f
  //   d d f f d d f f d d f f d d f f d d f f d d f f d d f f d d f f d d f f d d f f d d f f d d f f d d
  //   f f d d f f d d f f d d f f d d f f d d f f d d f f d d f f d d f f d d f f d d f f d d f f d d f f
  //   d d f f d d f f d d f f d d f f d d f f d d f f d d f f d d f f d d f f d d f f d d f f d d f f d d
  //   f f d d f f d d f f d d f f d d f f d d f f d d f f d d f f d d f f d d f f d d f f d d f f d d f f
  //   d d f f d d f f d d f f d d f f d d f f d d f f d d f f d d f f d d f f d d f f d d f f d d f f d d
  //   f f d d f f d d f f d d f f d d f f d d f f d d f f d d f f d d f f d d f f d d f f d d f f d d f f
  //   d d f f d d f f d d f f d d f f d d f f d d f f d d f f d d f f d d f f d d f f d d f f d d f f d d
  //   f f d d f f d d f f d d f f d d f f d d f f d d f f d d f f d d f f d d f f d d f f d d f f d d f f
  //   d d f f d d f f d d f f d d f f d d f f d d f f d d f f d d f f d d f f d d f f d d f f d d f f d d
  //   f f d d f f d d f f d d f f d d f f d d f f d d f f d d f f d d f f d d f f d d f f d d f f d d f f
  //   d d f f d d f f d d f f d d f f d d f f d d f f d d f f d d f f d d f f d d f f d d f f d d f f d d
  //   f f d d f f d d f f d d f f d d f f d d f f d d f f d d f f d d f f d d f f d d f f d d f f d d f f
  //   d d f f d d f f d d f f d d f f d d f f d d f f d d f f d d f f d d f f d d f f d d f f d d f f d d
  //   f f d d f f d d f f d d f f d d f f d d f f d d f f d d f f d d f f d d f f d d f f d d f f d d f f
  //   d d f f d d f f d d f f d d f f d d f f d d f f d d f f d d f f d d f f d d f f d d f f d d f f d d
  //   f f d d f f d d f f d d f f d d f f d d f f d d f f d d f f d d f f d d f f d d f f d d f f d d f f
  //   d d f f d d f f d d f f d d f f d d f f d d f f d d f f d d f f d d f f d d f f d d f f d d f f d d
  //   f f d d f f d d f f d d f f d d f f d d f f d d f f d d f f d d f f d d f f d d f f d d f f d d f f
  //   d d f f d d f f d d f f d d f f d d f f d d f f d d f f d d f f d d f f d d f f d d f f d d f f d d
  //   f f d d f f d d f f d d f f d d f f d d f f d d f f d d f f d d f f d d f f d d f f d d f f d d f f
  //   d d f f d d f f d d f f d d f f d d f f d d f f d d f f d d f f d d f f d d f f d d f f d d f f d d
  //   f f d d f f d d f f d d f f d d f f d d f f d d f f d d f f d d f f d d f f d d f f d d f f d d f f
  //   d d f f d d f f d d f f d d f f d d f f d d f f d d f f d d f f d d f f d d f f d d f f d d f f d d
  //   f f d d f f d d f f d d f f d d f f d d f f d d f f d d f f d d f f d d f f d d f f d d f f d d f f
  //   d d f f d d f f d d f f d d f f d d f f d d f f d d f f d d f f d d f f d d f f d d f f d d f f d d
  //   f f d d f f d d f f d d f f d d f f d d f f d d f f d d f f d d f f d d f f d d f f d d f f d d f f
  //   d d f f d d f f d d f f d d f f d d f f d d f f d d f f d d f f d d f f d d f f d d f f d d f f d d
  //   f f d d f f d d f f d d f f d d f f d d f f d d f f d d f f d d f f d d f f d d f f d d f f d d f f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
endmodule

module OctalTransceiver74245 (
  input  [7:0] B_in,
  input  NotEnable,
  input  Dir,
  input  [7:0] A_in,
  output [7:0] B_Out,
  output [7:0] A_out
);

  wire and_1_out, and_2_out, not_1_out, not_2_out, not_3_out;

  not not_1 (not_1_out, Dir);
  not not_2 (not_2_out, NotEnable);
  and and_1 (and_1_out, not_1_out, not_2_out);
  and and_2 (and_2_out, Dir, not_3_out);
  not not_3 (not_3_out, NotEnable);
  assign A_out[0] = and_1_out ? B_in[0] : 1'bz;  // Controlled_Buffer controlled_buffer_1
  assign A_out[1] = and_1_out ? B_in[1] : 1'bz;  // Controlled_Buffer controlled_buffer_2
  assign B_Out[0] = and_2_out ? A_in[0] : 1'bz;  // Controlled_Buffer controlled_buffer_3
  assign B_Out[1] = and_2_out ? A_in[1] : 1'bz;  // Controlled_Buffer controlled_buffer_4
  assign A_out[2] = and_1_out ? B_in[2] : 1'bz;  // Controlled_Buffer controlled_buffer_5
  assign A_out[3] = and_1_out ? B_in[3] : 1'bz;  // Controlled_Buffer controlled_buffer_6
  assign B_Out[2] = and_2_out ? A_in[2] : 1'bz;  // Controlled_Buffer controlled_buffer_7
  assign B_Out[3] = and_2_out ? A_in[3] : 1'bz;  // Controlled_Buffer controlled_buffer_8
  assign A_out[4] = and_1_out ? B_in[4] : 1'bz;  // Controlled_Buffer controlled_buffer_9
  assign A_out[5] = and_1_out ? B_in[5] : 1'bz;  // Controlled_Buffer controlled_buffer_10
  assign B_Out[4] = and_2_out ? A_in[4] : 1'bz;  // Controlled_Buffer controlled_buffer_11
  assign B_Out[5] = and_2_out ? A_in[5] : 1'bz;  // Controlled_Buffer controlled_buffer_12
  assign A_out[6] = and_1_out ? B_in[6] : 1'bz;  // Controlled_Buffer controlled_buffer_13
  assign A_out[7] = and_1_out ? B_in[7] : 1'bz;  // Controlled_Buffer controlled_buffer_14
  assign B_Out[6] = and_2_out ? A_in[6] : 1'bz;  // Controlled_Buffer controlled_buffer_15
  assign B_Out[7] = and_2_out ? A_in[7] : 1'bz;  // Controlled_Buffer controlled_buffer_16
endmodule

module Register8 (
  input  Clock,
  input  NotLoad,
  input  NotEnable,
  input  [7:0] BusIn,
  output [7:0] BusOut,
  output [7:0] DataOut
);

  OctalTransceiver74245 octaltransceiver74245_1 (
    .B_Out(BusOut), .A_out(DataOut), .Dir(1'b1), .NotEnable(NotEnable), .B_in(BusOut), .A_in(DataOut));
  _74377 #(.ShowInternalStructure("true")) u_74377_1 (
    .pin1(NotLoad), .pin2(DataOut[0]), .pin3(BusIn[0]), .pin4(BusIn[1]), .pin5(DataOut[1]),
    .pin6(DataOut[2]), .pin7(BusIn[2]), .pin8(BusIn[3]), .pin9(DataOut[3]), .pin19(DataOut[7]),
    .pin18(BusIn[7]), .pin17(BusIn[6]), .pin16(DataOut[6]), .pin15(DataOut[5]), .pin14(BusIn[5]),
    .pin13(BusIn[4]), .pin12(DataOut[4]), .pin11(Clock));
endmodule

module ProgramCounter (
  input  Clock,
  input  NotClear,
  input  NotLoad,
  input  Count,
  input  [15:0] AddressIn,
  output [15:0] AddressOut
);

  wire n74161_1_pin15, n74161_2_pin15, n74161_3_pin15;

  _74161 #(.ShowInternalStructure("true")) u_74161_1 (
    .pin1(NotClear), .pin2(Clock), .pin3(AddressIn[0]), .pin4(AddressIn[1]), .pin5(AddressIn[2]),
    .pin6(AddressIn[3]), .pin7(Count), .pin15(n74161_1_pin15), .pin14(AddressOut[0]), .pin13(AddressOut[1]),
    .pin12(AddressOut[2]), .pin11(AddressOut[3]), .pin10(NotLoad), .pin9(NotLoad));
  _74161 #(.ShowInternalStructure("true")) u_74161_2 (
    .pin1(NotClear), .pin2(Clock), .pin3(AddressIn[4]), .pin4(AddressIn[5]), .pin5(AddressIn[6]),
    .pin6(AddressIn[7]), .pin7(Count), .pin15(n74161_2_pin15), .pin14(AddressOut[4]), .pin13(AddressOut[5]),
    .pin12(AddressOut[6]), .pin11(AddressOut[7]), .pin10(n74161_1_pin15), .pin9(NotLoad));
  _74161 #(.ShowInternalStructure("true")) u_74161_3 (
    .pin1(NotClear), .pin2(Clock), .pin3(AddressIn[8]), .pin4(AddressIn[9]), .pin5(AddressIn[10]),
    .pin6(AddressIn[11]), .pin7(Count), .pin15(n74161_3_pin15), .pin14(AddressOut[8]), .pin13(AddressOut[9]),
    .pin12(AddressOut[10]), .pin11(AddressOut[11]), .pin10(n74161_2_pin15), .pin9(NotLoad));
  _74161 #(.ShowInternalStructure("true")) u_74161_4 (
    .pin1(NotClear), .pin2(Clock), .pin3(AddressIn[12]), .pin4(AddressIn[13]), .pin5(AddressIn[14]),
    .pin6(AddressIn[15]), .pin7(Count), .pin14(AddressOut[12]), .pin13(AddressOut[13]),
    .pin12(AddressOut[14]), .pin11(AddressOut[15]), .pin10(n74161_3_pin15), .pin9(NotLoad));  // open: pin15

  // Other names for the same wires on the sheet: Clk = Clock; nClr = NotClear; nLD = NotLoad
endmodule

module Bus16 (
  input  NotEnablePC,
  input  [7:0] PCHigh,
  input  [7:0] PCLow,
  input  NotEnableA,
  input  [7:0] AHigh,
  input  [7:0] ALow,
  output [15:0] RAMAddress
);

  OctalTransceiver74245 octaltransceiver74245_1 (
    .B_Out(PCHigh), .A_out(RAMAddress[15:8]), .Dir(1'b0), .NotEnable(NotEnablePC), .B_in(PCHigh),
    .A_in(RAMAddress[15:8]));
  OctalTransceiver74245 octaltransceiver74245_2 (
    .B_Out(PCLow), .A_out(RAMAddress[7:0]), .Dir(1'b0), .NotEnable(NotEnablePC), .B_in(PCLow),
    .A_in(RAMAddress[7:0]));
  OctalTransceiver74245 octaltransceiver74245_3 (
    .B_Out(AHigh), .A_out(RAMAddress[15:8]), .Dir(1'b0), .NotEnable(NotEnableA), .B_in(AHigh),
    .A_in(RAMAddress[15:8]));
  OctalTransceiver74245 octaltransceiver74245_4 (
    .B_Out(ALow), .A_out(RAMAddress[7:0]), .Dir(1'b0), .NotEnable(NotEnableA), .B_in(ALow),
    .A_in(RAMAddress[7:0]));
endmodule

module MemoryHelper (
  input  NotEnablePC,
  input  [7:0] PCHigh,
  input  [7:0] PCLow,
  input  NotEnableA,
  input  [7:0] AHigh,
  input  [7:0] ALow,
  output [15:0] RAMAddress
);

  OctalTransceiver74245 octaltransceiver74245_1 (
    .B_Out(PCHigh), .A_out(RAMAddress[15:8]), .Dir(1'b0), .NotEnable(NotEnablePC), .B_in(PCHigh),
    .A_in(RAMAddress[15:8]));
  OctalTransceiver74245 octaltransceiver74245_2 (
    .B_Out(PCLow), .A_out(RAMAddress[7:0]), .Dir(1'b0), .NotEnable(NotEnablePC), .B_in(PCLow),
    .A_in(RAMAddress[7:0]));
  OctalTransceiver74245 octaltransceiver74245_3 (
    .B_Out(AHigh), .A_out(RAMAddress[15:8]), .Dir(1'b0), .NotEnable(NotEnableA), .B_in(AHigh),
    .A_in(RAMAddress[15:8]));
  OctalTransceiver74245 octaltransceiver74245_4 (
    .B_Out(ALow), .A_out(RAMAddress[7:0]), .Dir(1'b0), .NotEnable(NotEnableA), .B_in(ALow),
    .A_in(RAMAddress[7:0]));
endmodule

module Microcode (
  input  NotClear,
  input  Clock,
  output A,
  output B
);

  wire n74163_1_pin7;

  _74163 u_74163_1 (
    .pin1(NotClear), .pin2(Clock), .pin7(n74163_1_pin7), .pin14(A), .pin13(B), .pin10(n74163_1_pin7),
    .pin9(n74163_1_pin7));  // open: pin3, pin4, pin5, pin6, pin15, pin12, pin11
  // also tied to VCC on the sheet: n74163_1_pin7
endmodule

module RAM_2 (
  input  Clock,
  input  [7:0] DataInL,
  input  WriteL,
  input  AddressL,
  input  AddressR,
  output [7:0] DataOutR,
  output [7:0] DataOutL
);

  wire decoder_1_out0, decoder_1_out1, not_1_out;
  wire [7:0] multiplexer_1_out, register_1_q, register_2_q;

  Decoder decoder_1 (.out0(decoder_1_out0), .out1(decoder_1_out1), .sel(AddressL), .en(WriteL));
  Register register_1 (.D(DataInL), .en(decoder_1_out0), .clk(Clock), .Q(register_1_q), .clr(1'b0));
  Register register_2 (.D(DataInL), .en(decoder_1_out1), .clk(Clock), .Q(register_2_q), .clr(1'b0));
  Multiplexer #(.width(8)) multiplexer_1 (
    .in0(register_1_q), .in1(register_2_q), .out(multiplexer_1_out), .sel(AddressL));
  Multiplexer #(.width(8)) multiplexer_2 (.in0(register_1_q), .in1(register_2_q), .out(DataOutR), .sel(AddressR));
  assign DataOutL = not_1_out ? multiplexer_1_out : 8'bz;  // Controlled_Buffer controlled_buffer_1
  not not_1 (not_1_out, WriteL);
endmodule

module RAM_4 (
  input  Clock,
  input  [7:0] DataInL,
  input  NotWriteL,
  input  [1:0] AddressL,
  input  [1:0] AddressR,
  output [7:0] DataOutL,
  output [7:0] DataOutR
);

  wire decoder_1_out0, decoder_1_out1, not_1_out;
  wire [7:0] multiplexer_1_out, ram_2_1_dataoutl, ram_2_1_dataoutr, ram_2_2_dataoutl, ram_2_2_dataoutr;

  not not_1 (not_1_out, NotWriteL);
  Decoder decoder_1 (.out0(decoder_1_out0), .out1(decoder_1_out1), .sel(AddressL[1]), .en(not_1_out));
  RAM_2 ram_2_1 (
    .Clock(Clock), .DataInL(DataInL), .WriteL(decoder_1_out0), .AddressL(AddressL[0]),
    .AddressR(AddressR[0]), .DataOutR(ram_2_1_dataoutr), .DataOutL(ram_2_1_dataoutl));
  RAM_2 ram_2_2 (
    .Clock(Clock), .DataInL(DataInL), .WriteL(decoder_1_out1), .AddressL(AddressL[0]),
    .AddressR(AddressR[0]), .DataOutR(ram_2_2_dataoutr), .DataOutL(ram_2_2_dataoutl));
  Multiplexer #(.width(8)) multiplexer_1 (
    .in0(ram_2_1_dataoutl), .in1(ram_2_2_dataoutl), .out(multiplexer_1_out), .sel(AddressL[1]));
  Multiplexer #(.width(8)) multiplexer_2 (
    .in0(ram_2_1_dataoutr), .in1(ram_2_2_dataoutr), .out(DataOutR), .sel(AddressR[1]));
  assign DataOutL = NotWriteL ? multiplexer_1_out : 8'bz;  // Controlled_Buffer controlled_buffer_1
endmodule

module RAM_IDT7134 (
  input  Clock,
  input  [7:0] DataInL,
  input  NotWriteRamL,
  input  [1:0] AddressL,
  input  [1:0] AddressR,
  input  NotOutputEnableL,
  input  NotOutputEnableR,
  output [7:0] DataOutL,
  output [7:0] DataOutR
);

  wire not_1_out, not_2_out;
  wire [7:0] ram_4_1_dataoutl, ram_4_1_dataoutr;

  RAM_4 ram_4_1 (
    .Clock(Clock), .DataInL(DataInL), .NotWriteL(NotWriteRamL), .AddressL(AddressL), .AddressR(AddressR),
    .DataOutL(ram_4_1_dataoutl), .DataOutR(ram_4_1_dataoutr));
  assign DataOutL = not_1_out ? ram_4_1_dataoutl : 8'bz;  // Controlled_Buffer controlled_buffer_1
  not not_1 (not_1_out, NotOutputEnableL);
  assign DataOutR = not_2_out ? ram_4_1_dataoutr : 8'bz;  // Controlled_Buffer controlled_buffer_2
  not not_2 (not_2_out, NotOutputEnableR);
endmodule

module fixed74181 (
  input  S1,
  input  S2,
  input  S3,
  input  S4,
  input  B4,
  input  A4,
  input  B3,
  input  A3,
  input  B2,
  input  A2,
  input  B1,
  input  A1,
  input  M,
  input  CIN,
  output G,
  output COUT,
  output P,
  output Y4,
  output Y3,
  output EQ,
  output Y2,
  output Y1
);

  wire and_1_out, and_2_out, and_3_out, and_4_out, and_5_out, and_6_out, and_7_out, and_8_out, and_9_out,
       and_10_out, and_11_out, and_12_out, and_13_out, and_14_out, and_15_out, and_16_out, and_17_out,
       and_18_out, and_19_out, and_20_out, and_21_out, and_22_out, and_23_out, and_24_out, and_25_out,
       and_26_out, and_27_out, and_28_out, buffer_1_out, buffer_2_out, buffer_3_out, buffer_4_out,
       buffer_5_out, nand_1_out, nand_3_out, nor_1_out, nor_2_out, nor_3_out, nor_4_out, nor_5_out,
       nor_6_out, nor_7_out, nor_8_out, nor_10_out, nor_11_out, nor_12_out, not_1_out, not_2_out, not_3_out,
       not_4_out, not_5_out, not_6_out, not_7_out, xor_1_out, xor_2_out, xor_3_out, xor_4_out;

  not not_1 (not_1_out, B4);
  not not_2 (not_2_out, B3);
  not not_3 (not_3_out, B2);
  not not_4 (not_4_out, B1);
  not not_5 (not_5_out, M);
  and and_1 (and_1_out, B4, S1, A4);
  and and_2 (and_2_out, A4, S2, not_1_out);
  and and_3 (and_3_out, not_1_out, S3);
  and and_4 (and_4_out, S4, B4);
  buf buffer_1 (buffer_1_out, A4);
  and and_5 (and_5_out, B3, S1, A3);
  and and_6 (and_6_out, A3, S2, not_2_out);
  and and_7 (and_7_out, not_2_out, S3);
  and and_8 (and_8_out, S4, B3);
  buf buffer_2 (buffer_2_out, A3);
  and and_9 (and_9_out, B2, S1, A2);
  and and_10 (and_10_out, A2, S2, not_3_out);
  and and_11 (and_11_out, not_3_out, S3);
  and and_12 (and_12_out, S4, B2);
  buf buffer_3 (buffer_3_out, A2);
  and and_13 (and_13_out, B1, S1, A1);
  and and_14 (and_14_out, A1, S2, not_4_out);
  and and_15 (and_15_out, not_4_out, S3);
  and and_16 (and_16_out, S4, B1);
  buf buffer_4 (buffer_4_out, A1);
  nor nor_1 (nor_1_out, and_1_out, and_2_out);
  nor nor_2 (nor_2_out, and_3_out, and_4_out, buffer_1_out);
  nor nor_3 (nor_3_out, and_5_out, and_6_out);
  nor nor_4 (nor_4_out, and_7_out, and_8_out, buffer_2_out);
  nor nor_5 (nor_5_out, and_9_out, and_10_out);
  nor nor_6 (nor_6_out, and_11_out, and_12_out, buffer_3_out);
  nor nor_7 (nor_7_out, and_13_out, and_14_out);
  nor nor_8 (nor_8_out, and_15_out, and_16_out, buffer_4_out);
  xor xor_1 (xor_1_out, nor_1_out, nor_2_out);
  xor xor_2 (xor_2_out, nor_3_out, nor_4_out);
  xor xor_3 (xor_3_out, nor_5_out, nor_6_out);
  xor xor_4 (xor_4_out, nor_7_out, nor_8_out);
  buf buffer_5 (buffer_5_out, nor_2_out);
  and and_17 (and_17_out, nor_1_out, nor_4_out);
  and and_18 (and_18_out, nor_1_out, nor_3_out, nor_6_out);
  and and_19 (and_19_out, nor_1_out, nor_3_out, nor_5_out, nor_8_out);
  nand nand_1 (nand_1_out, nor_1_out, nor_3_out, nor_5_out, nor_7_out, CIN);
  nand nand_2 (P, nor_1_out, nor_3_out, nor_5_out, nor_7_out);
  and and_20 (and_20_out, CIN, nor_7_out, nor_5_out, nor_3_out, not_5_out);
  and and_21 (and_21_out, nor_5_out, nor_3_out, nor_8_out, not_5_out);
  and and_22 (and_22_out, nor_3_out, nor_6_out, not_5_out);
  and and_23 (and_23_out, nor_4_out, not_5_out);
  and and_24 (and_24_out, CIN, nor_7_out, nor_5_out, not_5_out);
  and and_25 (and_25_out, nor_5_out, nor_8_out, not_5_out);
  and and_26 (and_26_out, nor_6_out, not_5_out);
  and and_27 (and_27_out, CIN, nor_7_out, not_5_out);
  and and_28 (and_28_out, nor_8_out, not_5_out);
  nand nand_3 (nand_3_out, CIN, not_5_out);
  nor nor_9 (G, buffer_5_out, and_17_out, and_18_out, and_19_out);
  nor nor_10 (nor_10_out, and_20_out, and_21_out, and_22_out, and_23_out);
  nor nor_11 (nor_11_out, and_24_out, and_25_out, and_26_out);
  nor nor_12 (nor_12_out, and_27_out, and_28_out);
  not not_6 (not_6_out, G);
  or or_1 (COUT, not_6_out, not_7_out);
  not not_7 (not_7_out, nand_1_out);
  xor xor_5 (Y4, xor_1_out, nor_10_out);
  xor xor_6 (Y3, xor_2_out, nor_11_out);
  xor xor_7 (Y2, xor_3_out, nor_12_out);
  xor xor_8 (Y1, xor_4_out, nand_3_out);
  and and_29 (EQ, Y3, Y4, Y1, Y2);
endmodule
